# Fritzing sketch reset_circuit_4 (saved by Fritzing 0.9.6b)
circuit board: 4.06402cm x 2.67001cm
breadboards: 1

parts:
  R1 = Resistor [tolerance=±5% power=0.25 resistance=10k package=THT]
  R2 = Resistor [tolerance=±5% power=0.25 resistance=10k package=THT]
  Q1 = NPN-Transistor [package="TO92 [THT]"]
  Q2 = NPN-Transistor [package="TO92 [THT]"]
  Q3 = NPN-Transistor [package="TO92 [THT]"]
  R7 = Resistor [tolerance=±5% power=0.25 resistance=10k package=THT]
  R8 = Resistor [tolerance=±5% power=0.25 resistance=1k package=THT]
  Pad1 = Pad [width=6.2841234556978485 height=2.5529572619324856 connect=center]
  Pad2 = Pad [width=6.2841234556978485 height=2.5529572619324856 connect=center]
  Pad3 = Pad [width=6.2841234556978485 height=2.5529572619324856 connect=center]
  Pad4 = Pad [width=6.2841234556978485 height=2.5529572619324856 connect=center]
  Pad5 = Pad [width=6.2841234556978485 height=2.5529572619324856 connect=center]
  R9 = Resistor [tolerance=±5% power=0.25 resistance=1k package=THT]

nets:
  PB1: R1.Pin_0, Pad1.pad
  N1: R1.Pin_1, Q1.B
  PB3: R2.Pin_0, Pad2.pad
  N2: R2.Pin_1, Q2.B
  GND: Q1.E, Q2.E, Q3.E, Pad5.pad
  N3: Q1.C, Q2.C, R7.Pin_0, R8.Pin_0, R9.Pin_1
  N4: Q3.B, R7.Pin_1
  RESET: Q3.C, R8.Pin_1, Pad3.pad
  5V: Pad4.pad, R9.Pin_0

notes:
  Q1
  Q2
  Q3
  10K
  1K
  GND
  VCC
  SIG2
  SIG1
  RESET
  JRB
  C64 RESET
  Q1,Q2,Q3 -> NPN
