# Fritzing sketch reset_circuit_3 (saved by Fritzing 0.9.3b)
circuit board: 7.57768cm x 1.95015cm
breadboards: 1

parts:
  R1 = Resistor [tolerance=±5% power=0.25 resistance=4.7k package=THT]
  R2 = Resistor [tolerance=±5% power=0.25 resistance=4.7k package=THT]
  Q1 = NPN-Transistor [package="TO92 [THT]"]
  Q2 = NPN-Transistor [package="TO92 [THT]"]
  R3 = Resistor [tolerance=±5% power=0.25 resistance=1k package=THT]
  R4 = Resistor [tolerance=±5% power=0.25 resistance=1k package=THT]
  U1 = 4011 4 x 2 Input NAND Gate, multi-part [part_number=4011 package="DIP (Dual Inline) [THT]"]
  Part1 = 4011_4_x_2_input_NAND_gate_multipart_subpart1 [part_number=4011]
  U1_1 = 4011_4_x_2_input_NAND_gate_multipart_subpart2 [part_number=4011]
  U1_2 = 4011_4_x_2_input_NAND_gate_multipart_subpart3 [part_number=4011]  # not connected
  LED1 = LED - 5mm [color="Red (633nm)" current=0.030 package="5 mm [THT]"]
  Q3 = NPN-Transistor [package="TO92 [THT]"]
  R7 = Resistor [tolerance=±5% power=0.25 resistance=4.7k package=THT]
  R8 = Resistor [tolerance=±5% power=0.25 resistance=1k package=THT]
  R9 = Resistor [tolerance=±5% power=0.25 resistance=4.7k package=THT]
  R10 = Resistor [tolerance=±5% power=0.25 resistance=4.7k package=THT]
  Pad1 = Pad [width=4.4480570815850857 height=1.4164051375291375 connect=center]
  Pad2 = Pad [width=4.4480570815850857 height=1.4164051375291375 connect=center]
  Pad3 = Pad [width=4.4480570815850857 height=1.4164051375291375 connect=center]
  Pad4 = Pad [width=1.5905479999999999 height=2.6511278222222221 connect=center]
  Pad5 = Pad [width=4.4480570815850857 height=1.4164051375291375 connect=center]
  Pad6 = Pad [width=4.4480570815850857 height=1.4164051375291375 connect=center]

nets:
  PB1: R1.Pin_0, Pad6.pad
  N1: R1.Pin_1, Q1.B
  PB3: R2.Pin_0, Pad5.pad
  N2: R2.Pin_1, Q2.B
  GND: Q1.E, Q2.E, U1.connector6, Part1.connector6, Q3.E, R9.Pin_1, R10.Pin_1, Pad2.pad
  N3: Q1.C, R3.Pin_1, U1.connector0, U1_1.connector0, R9.Pin_0
  N4: Q2.C, R4.Pin_0, U1.connector1, U1_1.connector1, R10.Pin_0
  5V: R3.Pin_0, R4.Pin_1, U1.connector4, U1.connector13, Part1.connector13, R8.Pin_0, Pad1.pad
  N5: U1.connector2, U1.connector3, Pad4.pad
  N6: U1.connector5, R7.Pin_0
  RESET: LED1.cathode, Q3.C, Pad3.pad
  N7: LED1.anode, R8.Pin_1
  N8: Q3.B, R7.Pin_1

notes:
  +
  gnd
  reset
  pb1
  pb3
  74LS00N
  R10
  R9
  R4
  R3
  R7
  R8
  LED1
  Q3
  Q1
  Q2
  R1
  R2
