# Fritzing sketch ay-pong-crystal_flipflop (saved by Fritzing 0.9.3b)
circuit board: 10cm x 8cm
breadboards: 1

parts:
  R1 = Rotary Potentiometer (Small) [maximum_resistance=100kΩ package=THT]
  R2 = Rotary Potentiometer (Small) [maximum_resistance=100kΩ package=THT]
  Power_plug1 = Power plug
  J1 = Screw terminal - 2 pins [package=THT]
  J2 = Screw terminal - 2 pins [package=THT]
  IC2 = IC, DIP package, 14 pins [chip_label=CD4072]
  R3 = Resistor [tolerance=±5% resistance=470 package=THT]
  R4 = Resistor [tolerance=±5% resistance=220 package=THT]
  R5 = Resistor [tolerance=±5% resistance=220 package=THT]
  R6 = Resistor [tolerance=±5% resistance=10k package=THT]
  R7 = Resistor [tolerance=±5% resistance=68k package=THT]
  C1 = Electrolytic Capacitor [capacitance=1µF package="100 mil [THT, electrolytic]"]
  C2 = Electrolytic Capacitor [capacitance=100nF package="100 mil [THT, electrolytic]"]
  C3 = Electrolytic Capacitor [capacitance=100nF package="100 mil [THT, electrolytic]"]
  S1 = Pushbutton [package="[THT]"]
  LED1 = LED - 5mm [color="Red (633nm)" package="5 mm [THT]"]
  SW1 = DIP SWITCH [package=dipswitch-02]
  SW2 = DIP SWITCH [package=dipswitch-02]
  R10 = Resistor [tolerance=±5% resistance=220 package=THT]
  R11 = Resistor [tolerance=±5% resistance=10k package=THT]
  R12 = Resistor [tolerance=±5% resistance=220 package=THT]
  R13 = Resistor [tolerance=±5% resistance=10k package=THT]
  C5 = Electrolytic Capacitor [capacitance=100nF package="100 mil [THT, electrolytic]"]
  C6 = Electrolytic Capacitor [capacitance=100nF package="100 mil [THT, electrolytic]"]
  J3 = female pin header, 2 pins [form="♀ (female)"]
  J4 = female pin header, 2 pins [form="♀ (female)"]
  J5 = female pin header, 2 pins [form="♀ (female)"]
  J6 = female pin header, 2 pins [form="♀ (female)"]
  IC1 = IC, DIP package, 28 pins [chip_label=AY-3-8500]
  J9 = female pin header, 2 pins [form="♀ (female)"]
  D2 = Zener Diode [part_number=1N4732A breakdown_voltage=5.1V package="300 mil [THT]"]
  R16 = Resistor [tolerance=±5% resistance=100 package=THT]
  R17 = Resistor [tolerance=±5% resistance=68 package=THT]
  U3 = crystal oscillator tht
  J10 = female pin header, 2 pins [form="♀ (female)"]
  Q1 = Basic FET P-Channel [package="TO220 [THT]"]
  R18 = Resistor [tolerance=±5% resistance=220 package=THT]
  C8 = Electrolytic Capacitor [capacitance=100nF package="100 mil [THT, electrolytic]"]
  C9 = Electrolytic Capacitor [capacitance=100nF package="100 mil [THT, electrolytic]"]
  U2 = 74HC595 [package="DIP16 [THT]"]

nets:
  N1: R1.leg1, R2.leg2, IC2.pin14, LED1.anode, IC1.pin4, R16.Pin_1, Q1.source, C8.+, C9.+
  N2: R1.wiper, R11.Pin_0
  GND: R1.leg2, R2.leg1, Power_plug1.GND, J1.pin1, J2.pin1, IC2.pin7, R5.Pin_0, R6.Pin_0, S1.Pin_3, S1.Pin_4, SW1.3, SW1.4, SW2.3, SW2.4, C5.-, C6.-, J3.pin2, J4.pin2, J5.pin2, J6.pin2, IC1.pin2, D2.anode, U3.Pin_7, Q1.drain, R18.Pin_0, C8.-, C9.-, U2.GND
  N3: R2.wiper, R13.Pin_1
  N4: Power_plug1.VCC, Q1.gate
  N5: J1.pin2, C1.-
  N6: J2.pin2, R17.Pin_0
  N7: IC2.pin1, R3.Pin_0
  N8: IC2.pin2, IC1.pin6
  N9: IC2.pin3, IC1.pin10
  N10: IC2.pin4, IC1.pin9
  N11: IC2.pin5, IC1.pin24
  N12: IC2.pin9, IC2.pin10, IC2.pin11, IC2.pin12, IC1.pin16
  N13: IC2.pin13, R4.Pin_0
  N14: R3.Pin_1, R4.Pin_1, R5.Pin_1, C2.-
  N15: R6.Pin_1, R7.Pin_1, C1.+
  N16: R7.Pin_0, IC1.pin3
  N17: C2.+, C3.+
  N18: C3.-, R17.Pin_1
  N19: S1.Pin_1, S1.Pin_2, IC1.pin25
  N20: LED1.cathode, R18.Pin_1
  N21: SW1.1, IC1.pin22
  N22: SW1.2, IC1.pin23
  N23: SW2.1, IC1.pin20
  N24: SW2.2, IC1.pin21
  N25: R10.Pin_0, IC1.pin12
  N26: R10.Pin_1, R11.Pin_1, C6.+
  N27: R12.Pin_0, R13.Pin_0, C5.+
  N28: R12.Pin_1, IC1.pin11
  N29: J3.pin1, IC1.pin5
  N30: J4.pin1, IC1.pin7
  N31: J5.pin1, IC1.pin8
  N32: J6.pin1, IC1.pin13
  N33: IC1.pin17, J9.pin2, J10.pin2
  N34: D2.cathode, R16.Pin_0, U3.Pin_14, U2.VCC
  N35: U3.Pin_8, J10.pin1

notes:
  THE PONG
  JRB, 2023.
  12-9 V (+)-
  AY-3-8500
  SN74LS175
  crystal osc
  CD4072
  75ohm
  220ohm
  330ohm
  510ohm
  10K
  68K
  100ohm
  5v1
  2Mhz or 4Mhz
  100nF
  1uF
  100uF

custom parts:
  crystal oscillator tht: Generic crystal oscillator tht.
